// Logisim project eldar_osmanovic_21053.circ as structural Verilog: 11 circuits, main circuit main
module main (
  input  in_1,
  input  in_2
);

  wire clock_1_out, incrementer_2_p2, incrementer_3_p1, incrementer_4_p1, isjal_1_i, isjr_1_jr,
       iszero_1_zero, maincontrol_1_alusrc, maincontrol_1_beq, maincontrol_1_bne, maincontrol_1_extop,
       maincontrol_1_j, maincontrol_1_memread, maincontrol_1_memtoreg, maincontrol_1_memwrite,
       maincontrol_1_regdest, nextpc_1_pcsrc, registerfile_1_p3;
  wire [1:0] register_1_q;
  wire [3:0] mips_alu_1_p3;
  wire [4:0] mipsprogramrom_1_p2_3, mipsprogramrom_1_p2_4, mipsprogramrom_1_p2_5, multiplexer_3_out,
       registerfile_1_p4;
  wire [5:0] mipsprogramrom_1_p2, mipsprogramrom_1_p2_6;
  wire [10:6] mipsprogramrom_1_p2_2;
  wire [29:0] incrementer_1_p2, multiplexer_1_out, nextpc_1_bjadresa, register_1_q_2;
  wire [31:0] extender_1_out_3, incrementer_5_p1, mips_alu_1_p5, mips_ram_1_p6, multiplexer_2_out,
       multiplexer_5_out, multiplexer_6_out, registerfile_1_p1, registerfile_1_p7, registerfile_1_p8;

  Multiplexer #(.width(30), .enable("false")) multiplexer_1 (
    .in0(incrementer_1_p2), .in1(nextpc_1_bjadresa), .out(multiplexer_1_out), .sel(nextpc_1_pcsrc));
  Multiplexer #(.width(32), .enable("false")) multiplexer_2 (
    .in0({multiplexer_1_out, register_1_q}), .in1(registerfile_1_p7), .out(multiplexer_2_out), .sel(isjr_1_jr));
  Register #(.width(32)) register_1 (
    .D(multiplexer_2_out), .en(in_1), .clk(clock_1_out), .Q({register_1_q_2, register_1_q}), .clr(in_2));
  Clock clock_1 (.out(clock_1_out));
  // Incrementer #(.width(30)) incrementer_1: pin names not known; wires that end beside it: register_1_q_2, incrementer_1_p2
  // Incrementer #(.width(32)) incrementer_2: pin names not known; wires that end beside it: {register_1_q_2, register_1_q}, incrementer_2_p2, incrementer_2_p2
  // Incrementer #(.width(32)) incrementer_3: pin names not known; wires that end beside it: incrementer_3_p1, incrementer_3_p1
  // Incrementer #(.width(32)) incrementer_4: pin names not known; wires that end beside it: incrementer_4_p1, incrementer_4_p1
  // Incrementer #(.width(32)) incrementer_5: pin names not known; wires that end beside it: incrementer_5_p1
  isJal isjal_1 (.opcode(mipsprogramrom_1_p2_6), .i(isjal_1_i));
  NextPC nextpc_1 (
    .incPC(incrementer_1_p2),
    .imm26({mipsprogramrom_1_p2_5, mipsprogramrom_1_p2_4, mipsprogramrom_1_p2_3, mipsprogramrom_1_p2_2, mipsprogramrom_1_p2}),
    .zero(iszero_1_zero), .beq(maincontrol_1_beq), .j(maincontrol_1_j), .bne(maincontrol_1_bne),
    .bjAdresa(nextpc_1_bjadresa), .PCsrc(nextpc_1_pcsrc));
  // MIPSProgramROM mipsprogramrom_1: pin names not known; wires that end beside it: {register_1_q_2, register_1_q}, {mipsprogramrom_1_p2_6, mipsprogramrom_1_p2_5, mipsprogramrom_1_p2_4, mipsprogramrom_1_p2_3, mipsprogramrom_1_p2_2, mipsprogramrom_1_p2}
  isJr isjr_1 (.func(mipsprogramrom_1_p2), .op(mipsprogramrom_1_p2_6), .jr(isjr_1_jr));
  Multiplexer #(.width(5), .enable("false")) multiplexer_3 (
    .in0(mipsprogramrom_1_p2_4), .in1(mipsprogramrom_1_p2_3), .out(multiplexer_3_out),
    .sel(maincontrol_1_regdest));
  // RegisterFile registerfile_1: pin names not known; wires that end beside it: registerfile_1_p1, clock_1_out, registerfile_1_p3, registerfile_1_p4, mipsprogramrom_1_p2_5, mipsprogramrom_1_p2_4, registerfile_1_p7, registerfile_1_p8
  Multiplexer #(.width(5), .enable("false")) multiplexer_4 (
    .in0(multiplexer_3_out), .in1({5{1'b1}}), .out(registerfile_1_p4), .sel(isjal_1_i));
  MainControl maincontrol_1 (
    .op(mipsprogramrom_1_p2_6), .RegDest(maincontrol_1_regdest), .RegWrite(registerfile_1_p3),
    .ExtOp(maincontrol_1_extop), .ALUsrc(maincontrol_1_alusrc), .Beq(maincontrol_1_beq),
    .Bne(maincontrol_1_bne), .J(maincontrol_1_j), .MemRead(maincontrol_1_memread),
    .MemWrite(maincontrol_1_memwrite), .MemToReg(maincontrol_1_memtoreg));
  Multiplexer #(.width(32), .enable("false")) multiplexer_5 (
    .in0(registerfile_1_p8), .in1(extender_1_out_3), .out(multiplexer_5_out), .sel(maincontrol_1_alusrc));
  Extender extender_1 (
    .imm({mipsprogramrom_1_p2_3, mipsprogramrom_1_p2_2, mipsprogramrom_1_p2}), .extOp(maincontrol_1_extop),
    .out_3(extender_1_out_3));
  // Mips_ALU mips_alu_1: pin names not known; wires that end beside it: registerfile_1_p7, multiplexer_5_out, mips_alu_1_p3, mipsprogramrom_1_p2_2, mips_alu_1_p5
  ALUcontrol alucontrol_1 (.func(mipsprogramrom_1_p2), .op(mipsprogramrom_1_p2_6), .ALUop(mips_alu_1_p3));
  isZero iszero_1 (.aluResult(mips_alu_1_p5), .zero(iszero_1_zero));
  // MIPS_RAM #(.addrWidth(24)) mips_ram_1: pin names not known; wires that end beside it: mips_alu_1_p5[23:0], registerfile_1_p8, maincontrol_1_memwrite, clock_1_out, maincontrol_1_memread, mips_ram_1_p6
  Multiplexer #(.width(32), .enable("false")) multiplexer_6 (
    .in0(mips_alu_1_p5), .in1(mips_ram_1_p6), .out(multiplexer_6_out), .sel(maincontrol_1_memtoreg));
  Multiplexer #(.width(32), .enable("false")) multiplexer_7 (
    .in0(multiplexer_6_out), .in1(incrementer_5_p1), .out(registerfile_1_p1), .sel(isjal_1_i));

  // Notes on the sheet:
  //   contents of mipsprogramrom_1 (hex, n*v repeats v):
  //   funkcija: subu $2, $4, $5 jr $31  main: addiu $8, $0, 4 ori $9, $0, 0xabcd sll $9, $9, 16 ori $9,
  //   $9, 0x1234 sw $9, 0($8) sw $9, 4($8) ori $10, $0, 4 addu $12, $8, $10 lw $13, 0($12) addu $5, $0,
  //   $13 addiu $4, $5, 8 jal funkcija sw $2, 8($8)
endmodule

module MainControl (
  input  [5:0] op,
  output RegDest,
  output RegWrite,
  output ExtOp,
  output ALUsrc,
  output Beq,
  output Bne,
  output J,
  output MemRead,
  output MemWrite,
  output MemToReg
);

  wire and_2_out, and_3_out, and_4_out, not_1_out, not_2_out, not_3_out, not_4_out, not_5_out, not_6_out,
       not_7_out, not_9_out, not_10_out, not_11_out, not_12_out, not_13_out, not_14_out, not_15_out;

  not not_1 (not_1_out, op[3]);
  not not_2 (not_2_out, op[1]);
  not not_3 (not_3_out, op[2]);
  not not_4 (not_4_out, op[1]);
  not not_5 (not_5_out, op[3]);
  not not_6 (not_6_out, op[2]);
  not not_7 (not_7_out, op[5]);
  not not_8 (ExtOp, op[2]);
  not not_9 (not_9_out, op[3]);
  not not_10 (not_10_out, op[0]);
  not not_11 (not_11_out, op[3]);
  not not_12 (not_12_out, op[1]);
  not not_13 (not_13_out, op[5]);
  not not_14 (not_14_out, op[3]);
  not not_15 (not_15_out, op[3]);
  and and_1 (RegDest, not_1_out, not_2_out);
  and and_2 (and_2_out, not_3_out, not_4_out);
  and and_3 (and_3_out, not_5_out, not_6_out, op[0]);
  and and_4 (and_4_out, not_7_out, op[3]);
  or or_1 (ALUsrc, op[1], op[3]);
  and and_5 (Beq, not_9_out, op[2], not_10_out);
  and and_6 (Bne, not_11_out, not_12_out, op[0]);
  and and_7 (J, not_13_out, not_14_out, op[1]);
  and and_8 (MemRead, op[5], not_15_out);
  and and_9 (MemWrite, op[5], op[3]);
  or or_2 (RegWrite, and_2_out, and_3_out, and_4_out);

  assign MemToReg = op[5];
endmodule

module ALU_R (
  input  [5:0] func,
  output [3:0] ALUop,
  output J
);

  wire not_1_out;

  and and_1 (ALUop[1], func[5], func[0]);
  not not_1 (not_1_out, func[5]);
  and and_2 (ALUop[0], not_1_out, func[0]);
  isJump isjump_1 (.f1(func[5]), .f2(func[4]), .f3(func[3]), .f4(func[2]), .f5(func[1]), .f6(func[0]), .J(J));

  assign ALUop[3:2] = func[2:1];
endmodule

module isJump (
  input  f1,
  input  f2,
  input  f3,
  input  f4,
  input  f5,
  input  f6,
  output J
);

  wire not_1_out, not_2_out, not_3_out, not_4_out, not_5_out;

  not not_1 (not_1_out, f1);
  not not_2 (not_2_out, f2);
  not not_3 (not_3_out, f4);
  not not_4 (not_4_out, f5);
  not not_5 (not_5_out, f6);
  and and_1 (J, not_1_out, not_2_out, f3, not_3_out, not_4_out, not_5_out);
endmodule

module ALU_I (
  input  o6,
  input  o5,
  input  o4,
  input  o3,
  input  o2,
  input  o1,
  output i4,
  output i3,
  output i2,
  output i1
);

  wire and_2_out, and_3_out, not_1_out, not_2_out, not_3_out, not_4_out, not_5_out;

  and and_1 (i4, o4, o3);
  not not_1 (not_1_out, o4);
  and and_2 (and_2_out, not_1_out, not_2_out);
  not not_2 (not_2_out, o2);
  and and_3 (and_3_out, o2, not_3_out);
  not not_3 (not_3_out, o1);
  not not_4 (not_4_out, o4);
  not not_5 (not_5_out, o3);
  or or_1 (i2, not_4_out, not_5_out, o1);
  or or_2 (i3, and_2_out, and_3_out);

  assign i1 = 1'b0;
endmodule

module ALUcontrol (
  input  [5:0] func,
  input  [5:0] op,
  output [3:0] ALUop
);

  wire alu_r_1_j, nor_1_out;
  wire [3:0] alu_i_1_i1, alu_r_1_aluop;

  ALU_R alu_r_1 (.func(func), .ALUop(alu_r_1_aluop), .J(alu_r_1_j));
  nor nor_1 (nor_1_out, op[0], op[1], op[2], op[3], op[4], op[5]);
  ALU_I alu_i_1 (
    .o6(op[5]), .o5(op[4]), .o4(op[3]), .o3(op[2]), .o2(op[1]), .o1(op[0]), .i4(alu_i_1_i1[3]),
    .i3(alu_i_1_i1[2]), .i2(alu_i_1_i1[1]), .i1(alu_i_1_i1[0]));
  Multiplexer #(.width(4), .enable("false")) multiplexer_1 (
    .in0(alu_i_1_i1), .in1(alu_r_1_aluop), .out(ALUop), .sel(nor_1_out));

  // Notes on the sheet:
  //   nije potrebno
endmodule

module Extender (
  input  [15:0] imm,
  input  extOp,
  output [31:0] out_3
);

  wire [31:0] bit_extender_1_out, bit_extender_2_out;

  assign bit_extender_1_out = {{16{imm[15]}}, imm};  // Bit_Extender bit_extender_1
  assign bit_extender_2_out = {{16{1'b0}}, imm};  // Bit_Extender bit_extender_2
  Multiplexer #(.width(32), .enable("false")) multiplexer_1 (
    .in0(bit_extender_2_out), .in1(bit_extender_1_out), .out(out_3), .sel(extOp));
endmodule

module NextPC (
  input  [29:0] incPC,
  input  [25:0] imm26,
  input  zero,
  input  beq,
  input  j,
  input  bne,
  output [29:0] bjAdresa,
  output PCsrc
);

  wire and_1_out, and_2_out;
  wire [29:0] adder_1_out, bit_extender_1_out;

  assign bit_extender_1_out = {{14{imm26[15]}}, imm26[15:0]};  // Bit_Extender bit_extender_1
  Adder #(.width(30)) adder_1 (.a(incPC), .b(bit_extender_1_out), .out(adder_1_out));  // open: cin, cout
  Multiplexer #(.width(30), .enable("false")) multiplexer_1 (
    .in0(adder_1_out), .in1({incPC[29:26], imm26}), .out(bjAdresa), .sel(j));
  and and_1 (and_1_out, ~zero, bne);  // AND_Gate
  or or_1 (PCsrc, and_1_out, j, and_2_out);
  and and_2 (and_2_out, zero, beq);
endmodule

module isZero (
  input  [31:0] aluResult,
  output zero
);

  nor nor_1 (zero, aluResult[0], aluResult[1], aluResult[2], aluResult[3], aluResult[4], aluResult[5], aluResult[6], aluResult[7], aluResult[8], aluResult[9], aluResult[10], aluResult[11], aluResult[12], aluResult[13], aluResult[14], aluResult[15], aluResult[17], aluResult[18], aluResult[19], aluResult[20], aluResult[21], aluResult[22], aluResult[23], aluResult[24], aluResult[25], aluResult[26], aluResult[27], aluResult[28], aluResult[29], aluResult[30], aluResult[31], aluResult[16]);
endmodule

module isJal (
  input  [5:0] opcode,
  output i
);

  wire not_1_out, not_2_out, not_3_out, not_4_out;

  not not_1 (not_1_out, opcode[5]);
  not not_2 (not_2_out, opcode[4]);
  not not_3 (not_3_out, opcode[3]);
  not not_4 (not_4_out, opcode[2]);
  and and_1 (i, not_1_out, not_2_out, not_3_out, not_4_out, opcode[1], opcode[0]);
endmodule

module isJr (
  input  [5:0] func,
  input  [5:0] op,
  output jr
);

  wire and_1_out, nor_1_out, not_1_out, not_2_out, not_3_out, not_4_out, not_5_out;

  nor nor_1 (nor_1_out, op[0], op[1], op[2], op[4], op[5], op[3]);
  not not_1 (not_1_out, func[5]);
  not not_2 (not_2_out, func[4]);
  not not_3 (not_3_out, func[2]);
  not not_4 (not_4_out, func[1]);
  not not_5 (not_5_out, func[0]);
  and and_1 (and_1_out, not_1_out, not_2_out, func[3], not_3_out, not_4_out, not_5_out);
  and and_2 (jr, and_1_out, nor_1_out);
endmodule
